# Fritzing sketch pi-zero-thermostat (saved by Fritzing 0.9.8b)

parts:
  MCU1 = Raspberry Pi Zero
  RHT1 = Humidity and Temperature Sensor RHT03
  R1 = Resistor [tolerance=±5% resistance=4.7 package="2512 [SMD]"]
  KY-1 = Keyes Relay [package=THT]

nets:
  N1: MCU1.pin_1, MCU1.pin_17, RHT1.Vcc, R1.Pin_1, KY-1.power
  N2: MCU1.pin_6, MCU1.pin_9, MCU1.pin_39, RHT1.GND_2, KY-1.ground
  N3: MCU1.pin_7, RHT1.Data-signal, R1.Pin_0
  N4: MCU1.pin_11, KY-1.signal
  N5: KY-1.C, KY-1.NO

custom parts:
  Keyes Relay: The Keyes 5V relay module is suitable for SCM development, home appliance control. It uses a 5V~12V TIL control signal which can control DC / AC signal.
